# Fritzing sketch Motor (saved by Fritzing 0.9.3b)
circuit board: 19.5cm x 9.39141cm
breadboards: 1

parts:
  U3 = atmega328 [package=dip]
  D1 = Resistor [tolerance=±5% resistance=220 part_number=4148 package=THT]
  +_- = LED - 5mm [color="Red (633nm)" package="5 mm [THT]"]
  +_-_2 = LED - 5mm [color="Red (633nm)" package="5 mm [THT]"]
  D4 = Resistor [tolerance=±5% resistance=4.7k package=THT]
  C7 = Capacitor Polarized [package=cpol-radial-1000uf-25v]
  R1 = Resistor [tolerance=±5% resistance=1k package=THT]
  R4 = Resistor [tolerance=±5% resistance=4.7k package=THT]
  J48 = rounded female pin header, 4 pins [form="♀ (female rounded)"]
  J58 = rounded female pin header, 3 pins [form="♀ (female rounded)"]
  XTAL = Crystal [frequency="16 Mhz" package=THT]
  R15 = Resistor [tolerance=±5% resistance=220 package=THT]
  Q1 = NPN-Transistor [package="TO92 [THT]"]
  R6 = Resistor [tolerance=±5% resistance=4.7k package=THT]
  Q5 = NPN-Transistor [package="TO92 [THT]"]
  C6 = Ceramic Capacitor [capacitance="100 nF" package="100 mil [THT, multilayer]"]
  C5 = Ceramic Capacitor [capacitance="100 nF" package="100 mil [THT, multilayer]"]
  RL1 = OMRON PCB Power Relay – G5LE [part_number="G5LE-1\n" package=THT]
  Q3 = TLP621 [package=THT]
  D2 = Resistor [tolerance=±5% resistance=220 package=THT]
  Q2 = NPN-Transistor [package="TO92 [THT]"]
  R3 = Resistor [tolerance=±5% resistance=4.7k package=THT]
  R2 = Resistor [tolerance=±5% resistance=4.7k package=THT]
  +_-_3 = LED - 5mm [color="Red (633nm)" package="5 mm [THT]"]
  U2 = Voltage Regulator - Variable [package="TO220 [THT]"]
  U1 = Voltage Regulator - Variable [package="TO220 [THT]"]
  + = screw terminal, 2 pins
  R13 = Resistor [tolerance=±5% resistance=4.7k package=THT]
  R12 = Resistor [tolerance=±5% resistance=4.7k package=THT]
  R10 = Resistor [tolerance=±5% resistance=4.7k package=THT]
  C11 = Resistor [tolerance=±5% resistance=220 package=THT]
  D3 = DIODE-ZENER [package=diode-zener]
  R14 = Resistor [tolerance=±5% resistance=4.7k package=THT]
  R16 = Resistor [tolerance=±5% resistance=4.7k package=THT]
  C4 = Ceramic Capacitor [capacitance="100 nF" package="100 mil [THT, multilayer]"]
  D5 = Resistor [tolerance=±5% resistance=4.7k package=THT]
  C8 = Ceramic Capacitor [capacitance="100 nF" package="100 mil [THT, multilayer]"]
  R11 = Resistor [tolerance=±5% resistance=4.7k package=THT]
  G1 = Graetz Bridge Rectifier [package="DIP (Dual Inline) [THT]"]
  Q7 = TLP621 [package=THT]
  C2 = Electrolytic Capacitor [capacitance=47µF voltage=20V package="100 mil [THT, electrolytic]"]
  RL2 = OMRON PCB Power Relay – G5LE [part_number="G5LE-1\n" package=THT]
  C1 = Electrolytic Capacitor [capacitance=47µF voltage=20V package="100 mil [THT, electrolytic]"]
  R19 = Resistor [tolerance=±5% resistance=4.7k package=THT]
  R18 = Resistor [tolerance=±5% resistance=4.7k package=THT]
  JP1 = Header 4 [package=jst-4-pth]
  Q8 = TLP621 [package=THT]
  SIM800L_CUSTOM2 = SIM800L_CUSTOM
  R5 = Resistor [tolerance=±5% resistance=4.7k package=THT]
  C3 = Ceramic Capacitor [capacitance="100 nF" package="100 mil [THT, multilayer]"]
  C9 = Ceramic Capacitor [capacitance="100 nF" package="100 mil [THT, multilayer]"]
  Q7_2 = MOSFET-NCHANNEL [package=sot23-3]
  Q4 = Sharp PC817 [package=THT]
  Q9 = TLP621 [package=THT]
  R20 = Resistor [tolerance=±5% resistance=4.7k package=THT]
  R_Y = screw terminal, 2 pins
  JP4 = Header 3 [package=jst-3-pth]
  JP3 = Header 2 [package=jst-2-pth]
  C10 = Capacitor Polarized [package=cpol-radial-1000uf-25v]
  JP4_2 = Header 2 [package=jst-2-pth]
  R8 = Resistor [tolerance=±5% resistance=4.7k package=THT]
  R9 = Resistor [tolerance=±5% resistance=4.7k package=THT]
  JP2 = Header 2 [package=jst-2-pth]
  Q6 = NPN-Transistor [package="TO92 [THT]"]
  R7 = Resistor [tolerance=±5% resistance=4.7k package=THT]
  R17 = Resistor [tolerance=±5% resistance=4.7k package=THT]
  R21 = Resistor [tolerance=±5% resistance=56k package=THT]
  R22 = Resistor [tolerance=±5% resistance=56k package=THT]
  R24 = Resistor [tolerance=±5% resistance=56k package=THT]
  R26 = Resistor [tolerance=±5% resistance=56k package=THT]
  R28 = Resistor [tolerance=±5% resistance=56k package=THT]
  R23 = Resistor [tolerance=±5% resistance=56k package=THT]
  R25 = Resistor [tolerance=±5% resistance=22k package=THT]
  R27 = Resistor [tolerance=±5% resistance=22k package=THT]
  M1 = V18ZA2P [package=v18za2p]
  M2 = V18ZA2P [package=v18za2p]
  D6 = Diode [package=diode-1n4001]
  D7 = Diode [package=diode-1n4001]
  J63 = female pin header, 4 pins [form="♀ (female)"]
  B_Y_R = female pin header, 3 pins [form="♀ (female)"]
  C_START_STOP = screw terminal, 3 pins

nets:
  N1: U3.RESET, R4.Pin_1, J48.pin1
  N2: U3.D0_(RX), J48.pin2, SIM800L_CUSTOM2.PIN_5
  N3: U3.D1_(TX), J48.pin3, SIM800L_CUSTOM2.PIN_4
  N4: U3.D2, U3.GND, C7.-, R15.Pin_1, Q1.E, Q5.E, C6.0, C5.1, Q2.E, +.pin1, R13.Pin_1, R10.Pin_1, C11.Pin_1, R16.Pin_0, C4.0, C8.0, G1.dc_negative, Q7.Pin_3, C2.-, C1.-, Q8.Pin_3, SIM800L_CUSTOM2.PIN_6, R5.Pin_0, C3.1, C9.0, Q9.Pin_2, Q9.Pin_3, C10.-, R9.Pin_1
  N5: U3.D3_(PWM), R6.Pin_1
  N6: U3.VCC, U3.AVCC, U3.AREF, D1.Pin_0, C7.+, R4.Pin_0, RL1.COIL2, Q3.Pin_3, D2.Pin_1, R3.Pin_1, U1.OUT, R14.Pin_0, C4.1, C8.1, RL2.COIL1, SIM800L_CUSTOM2.PIN2, C3.0, C9.1, Q4.Pin_4
  N7: U3.XLAT1, XTAL.pin_0, C5.0
  N8: U3.XLAT2, XTAL.pin_1, C6.1
  N9: U3.D5_(PWM), J58.pin1
  N10: U3.D6_(PWM), J58.pin2
  N11: U3.D7, J58.pin3
  N12: U3.D9_(PWM), R18.Pin_0
  N13: U3.D10_(PWM), R19.Pin_0
  N14: U3.D11_(PWM), R20.Pin_1
  N15: U3.A2, JP4_2.2
  N16: U3.A3, JP4_2.1
  N17: U3.A4, +_-_2.cathode
  N18: U3.A5, +_-_3.cathode
  N19: D1.Pin_1, Q1.C, RL1.COIL1
  N20: +_-.cathode, R16.Pin_1
  N21: +_-.anode, D4.Pin_1, R15.Pin_0, U2.IN, C11.Pin_0, D5.Pin_1, Q7_2.G, R17.Pin_1
  N22: +_-_2.anode, Q4.Pin_2
  N23: D4.Pin_0, G1.dc_positive, C10.+
  N24: R1.Pin_0, Q1.B
  N25: R1.Pin_1, Q4.Pin_3
  N26: R6.Pin_0, Q5.B
  N27: Q5.C, SIM800L_CUSTOM2.PIN_8
  N28: RL1.A, C_START_STOP.pin2
  N29: RL1.C, RL2.C, C_START_STOP.pin1
  N30: Q3.Pin_1, R3.Pin_0, Q4.Pin_1
  N31: Q3.Pin_2, +_-_3.anode
  N32: Q3.Pin_4, R2.Pin_0
  N33: D2.Pin_0, Q2.C, RL2.COIL2
  N34: Q2.B, R2.Pin_1
  N35: U2.ADJ, R12.Pin_1, R10.Pin_0
  N36: U2.OUT, R12.Pin_0, R11.Pin_1
  N37: U1.ADJ, R13.Pin_0, R14.Pin_1
  N38: U1.IN, D5.Pin_0, Q7_2.D
  N39: +.pin2, Q7_2.S, R8.Pin_0, Q6.C
  N40: D3.C, Q6.E
  N41: D3.A, R11.Pin_0
  N42: G1.ac_input_1, JP3.2
  N43: G1.ac_input_2, JP3.1
  N44: Q7.Pin_1, JP1.2
  N45: Q7.Pin_2, JP1.1
  N46: Q7.Pin_4, C2.+, R18.Pin_1
  N47: RL2.B, C_START_STOP.pin3
  N48: C1.+, R19.Pin_1, Q8.Pin_4
  N49: JP1.3, Q8.Pin_2
  N50: JP1.4, Q8.Pin_1
  N51: SIM800L_CUSTOM2.PIN_7, R5.Pin_1
  N52: Q9.Pin_1, R17.Pin_0
  N53: Q9.Pin_4, R20.Pin_0
  N54: R_Y.pin1, JP4.1
  N55: R_Y.pin2, JP4.3
  N56: R8.Pin_1, R9.Pin_0, JP2.2
  N57: JP2.1, R7.Pin_1
  N58: Q6.B, R7.Pin_0
  N59: R21.Pin_0, R24.Pin_0, B_Y_R.pin3
  N60: R21.Pin_1, M1.P$2, D6.C
  N61: R22.Pin_0, B_Y_R.pin2
  N62: R22.Pin_1, R26.Pin_0, M1.P$1
  N63: R24.Pin_1, R28.Pin_0, M2.P$1
  N64: R26.Pin_1, J63.pin3
  N65: R28.Pin_1, J63.pin1
  N66: R23.Pin_0, B_Y_R.pin1
  N67: R23.Pin_1, M2.P$2, D7.C
  N68: R25.Pin_0, J63.pin4
  N69: R25.Pin_1, D6.A
  N70: R27.Pin_0, J63.pin2
  N71: R27.Pin_1, D7.A

notes:
  M-
  RX
  TX
  DTR
  RST
  STX
  SRX
  1
  C
  MOTOR
  l
  FeedBack
  -
  Battery

custom parts:
  Graetz Bridge Rectifier: Graetz Bridge Rectifier - znany także jako Mostek Graetz'a :)
