# Fritzing sketch Motor Test Sketch (saved by Fritzing 0.9.3b)
circuit board: 18.5cm x 8.5cm
breadboards: 1

parts:
  R21 = Resistor [tolerance=±5% resistance=10k package=THT]
  XTAL = Crystal [frequency="16 Mhz" package=THT]
  R22 = Resistor [tolerance=±5% resistance=1k package=THT]
  Q1 = NPN-Transistor [part_number=2N2222A package="TO92 [THT]"]
  C6 = Ceramic Capacitor [capacitance=22pF package="100 mil [THT, multilayer]"]
  C5 = Ceramic Capacitor [capacitance=22pF package="100 mil [THT, multilayer]"]
  -_+ = screw terminal, 2 pins
  C7 = Ceramic Capacitor [capacitance="100 nF" package="100 mil [THT, multilayer]"]
  C8 = Electrolytic Capacitor [capacitance=33µF voltage=25V package="100 mil [THT, electrolytic]"]
  R3 = Resistor [tolerance=±5% resistance=1k package=THT]
  R23 = Resistor [tolerance=±5% resistance=1k package=THT]
  C11 = Ceramic Capacitor [capacitance="100 nF" package="100 mil [THT, multilayer]"]
  C13 = Ceramic Capacitor [capacitance="100 nF" package="100 mil [THT, multilayer]"]
  Q8 = MOSFET-NCHANNEL [part_number=AO3415 package=sot23-3]
  R38 = Resistor [tolerance=±5% resistance=56k package=THT]
  R40 = Resistor [tolerance=±5% resistance=22k package=THT]
  R39 = Resistor [tolerance=±5% resistance=56k package=THT]
  R41 = Resistor [tolerance=±5% resistance=22k package=THT]
  M2 = SIM800L_20MM
  J48 = rounded female pin header, 2 pins [form="♀ (female rounded)"]
  RESET1 = Pushbutton [package="[THT]"]
  PW2 = 2PTH JST FROM HEADER 5 [form="♀ (female rounded)" package=THT]
  C2 = Electrolytic Capacitor [capacitance=0.47mF voltage=10V package="200 mil [THT, electrolytic]"]
  R24 = Resistor [tolerance=±5% resistance=1k package=THT]
  C1 = Capacitor Polarized [package=cpol-radial-1000uf-25v]
  R9 = Resistor [tolerance=±5% resistance=3.3k package=THT]
  R8 = Resistor [tolerance=±5% resistance=5.6k package=THT]
  Q5 = Sharp PC817 [package=THT]
  Q4 = NPN-Transistor [part_number=2N2222A package="TO92 [THT]"]
  R1 = Resistor [tolerance=±5% resistance=1k package=THT]
  R2 = Resistor [tolerance=±5% resistance=1k package=THT]
  Q6 = Sharp PC817 [package=THT]
  Q3 = NPN-Transistor [part_number=2N2222A package="TO92 [THT]"]
  R19 = Resistor [tolerance=±5% resistance=1k package=THT]
  J2 = 3pth XH JST Custom [form="♀ (female rounded)" package=THT]
  J79 = rounded female pin header, 2 pins [form="♀ (female rounded)"]
  R20 = Resistor [tolerance=±5% resistance=1k package=THT]
  LED1 = LED - 3mm [color="Red (633nm)" package="3 mm [THT]"]
  R_B = screw terminal, 2 pins
  R36 = Resistor [tolerance=±5% resistance=150k package=THT]
  R_Y_B = screw terminal, 3 pins
  R32 = Resistor [tolerance=±5% resistance=150k package=THT]
  R33 = Resistor [tolerance=±5% resistance=15k package=THT]
  R34 = Resistor [tolerance=±5% resistance=68k package=THT]
  R35 = Resistor [tolerance=±5% resistance=150k package=THT]
  C14 = Capacitor [part_number=0.047uF package=cap-pth-large]
  R37 = Resistor [tolerance=±5% resistance=150k package=THT]
  C15 = Capacitor [part_number=0.047uF package=cap-pth-large]
  PW1 = 3pth XH JST Custom [form="♀ (female rounded)" package=THT]
  Q9 = MOSFET-NCHANNEL [part_number=AO3415 package=sot23-3]
  U1 = MOV [package=v18za2p]
  R42 = Resistor [tolerance=±5% resistance=22k package=THT]
  M3 = MP1584 Step Down Module [part_number=MP1584]
  ON/OFF_SW = Push Button Switch [package=os]
  D7 = Diode [package=diode-1n4001]
  R5 = Resistor [tolerance=±5% resistance=500 package=THT]
  Q7 = Sharp PC817 [package=THT]
  C4 = Ceramic Capacitor [capacitance="100 nF" package="100 mil [THT, multilayer]"]
  C17 = Ceramic Capacitor [capacitance="100 nF" package="100 mil [THT, multilayer]"]
  R28 = Resistor [tolerance=±5% resistance=10k package=THT]
  R17 = Resistor [tolerance=±5% resistance=10k package=THT]
  R13 = Resistor [tolerance=±5% resistance=2.2k package=THT]
  R16 = Resistor [tolerance=±5% resistance=3.3k package=THT]
  O1 = LM339 [package="DIP (Dual Inline) [THT]"]
  D8 = Diode [part_number="2V7 Zener Diode" package=diode-1n4148]
  R11 = Resistor [tolerance=±5% resistance=2.2k package=THT]
  R10 = Resistor [tolerance=±5% resistance=10k package=THT]
  R15 = Resistor [tolerance=±5% resistance=10k package=THT]
  R4 = Resistor [tolerance=±5% resistance=1k package=THT]
  C9 = Electrolytic Capacitor [capacitance=33µF voltage=25V package="100 mil [THT, electrolytic]"]
  R6 = Resistor [tolerance=±5% resistance=10k package=THT]
  C3 = Ceramic Capacitor [capacitance="100 nF" package="100 mil [THT, multilayer]"]
  R7 = Resistor [tolerance=±5% resistance=0 package=THT]
  R12 = Resistor [tolerance=±5% resistance=3.3k package=THT]
  D3 = Diode [part_number=SS34 package=sma-diode]
  R25 = Resistor [tolerance=±5% resistance=0 package=THT]
  R14 = Resistor [tolerance=±5% resistance=10k package=THT]
  Q2 = NPN-Transistor [part_number=2N2222A package="TO92 [THT]"]
  R27 = Resistor [tolerance=±5% resistance=10k package=THT]
  BRST = Pushbutton [package="[THT]"]
  R30 = Resistor [tolerance=±5% resistance=0 package=THT]  # not connected
  Battery_SW = Push Button Switch [package=os]
  Pad2 = Pad [width=3.9238365597985441 height=5 connect=center]
  Pad3 = Pad [width=7.0436313215666164 height=11 connect=center]
  Pad4 = Pad [width=9.5504079707572647 height=8.164131194932768 connect=center]
  Pad5 = Pad [width=12.885508902224791 height=9.0236541434622968 connect=center]
  R18 = Resistor [tolerance=±5% resistance=10k package=THT]
  R29 = Resistor [tolerance=±5% resistance=10k package=THT]
  R26 = Resistor [tolerance=±5% resistance=10k package=THT]
  J89 = rounded female pin header, 2 pins [form="♀ (female rounded)"]
  J91 = rounded female pin header, 2 pins [form="♀ (female rounded)"]
  J92 = rounded female pin header, 2 pins [form="♀ (female rounded)"]
  M1 = LM2596 Step Down Module
  J93 = rounded female pin header, 2 pins [form="♀ (female rounded)"]
  J58 = rounded female pin header, 4 pins [form="♀ (female rounded)"]
  U2 = atmega328 [package=dip]
  J1 = 3pth XH JST Custom [form="♀ (female rounded)" package=THT]
  J1_2 = 3pth XH JST Custom [form="♀ (female rounded)" package=THT]
  J3 = 4pth XH JST CUSTOM [form="♀ (female rounded)" package=THT]
  D2 = Diode [part_number=SS34 package=sma-diode]
  C10 = Electrolytic Capacitor [capacitance=33µF voltage=25V package="100 mil [THT, electrolytic]"]
  D1 = Diode [part_number=SS34 package=sma-diode]
  G1 = Rectifier_6A [package=THT]
  C12 = Electrolytic Capacitor [capacitance=47µF voltage=20V package="100 mil [THT, electrolytic]"]
  M4 = TP4056 Lithium Ion Battery Charger
  Fuse1 = Fuse with Handler
  D4 = Diode [part_number=SS34 package=sma-diode]
  R31 = Resistor [tolerance=±5% resistance=0 package=THT]
  J2_2 = 3pth XH JST Custom [form="♀ (female rounded)" package=THT]
  D6 = Diode [package=diode-1n4148]
  D5 = Diode [package=diode-1n4148]
  STOP = OMRON PCB Power Relay – G5LE [part_number="G5LE-1\n" package=THT]
  START = OMRON PCB Power Relay – G5LE [part_number="G5LE-1\n" package=THT]
  S1_S2_N1_N2 = screw terminal, 4 pins
  Pad6 = Pad [width=9.0241975461730455 height=8.3222272903273407 connect=center]
  Pad8 = Pad [width=14.733930963785852 height=10.251240952557273 connect=center]
  Pad9 = Pad [width=9 height=7 connect=center]
  Pad10 = Pad [width=6.5778288313715967 height=5.8355085372545954 connect=center]
  Pad11 = Pad [width=6.6275535259346015 height=8.5586621362824502 connect=center]
  Pad12 = Pad [width=5.3100184819903067 height=8.276154637045698 connect=center]
  Pad13 = Pad [width=8 height=4.3899999999999997 connect=center]
  Pad14 = Pad [width=8 height=4.3899999999999997 connect=center]
  G2 = Graetz Bridge Rectifier [package="DIP (Dual Inline) [THT]"]
  C16 = Electrolytic Capacitor [capacitance=33µF voltage=25V package="100 mil [THT, electrolytic]"]

nets:
  N1: R21.Pin_0, C7.1, C11.1, C13.1, M2.PIN2, C2.+, R9.Pin_1, Q9.D, R11.Pin_1, R10.Pin_1, R7.Pin_0, R12.Pin_1, J93.pin1, J93.pin2, U2.VCC, U2.AVCC, U2.AREF, C12.+, R31.Pin_0, R31.Pin_1
  N2: R21.Pin_1, RESET1.Pin_1, RESET1.Pin_2, U2.RESET
  N3: XTAL.pin_0, C5.0, U2.XLAT1
  N4: XTAL.pin_1, C6.1, U2.XLAT2
  N5: R22.Pin_0, Q1.B
  N6: R22.Pin_1, U2.D4
  N7: Q1.C, M2.PIN_8
  N8: C5.1, C7.0, U2.GND#7
  N9: -_+.pin1, M4.B+, D4.C
  N10: -_+.pin2, Fuse1.C1
  N11: C8.+, R3.Pin_1, C4.0, J1.pin3
  N12: R3.Pin_0, U2.D11_(PWM)
  N13: R23.Pin_0, M2.PIN_7
  N14: R23.Pin_1, U2.D2
  N15: C11.0, U2.GND#21
  N16: C13.0, M2.PIN_6
  N17: Q8.G, R28.Pin_0, R25.Pin_0
  N18: Q8.S, Q9.S, R28.Pin_1, D3.C, BRST.Pin_3, BRST.Pin_4, R26.Pin_1
  N19: Q8.D, M4.OUT+
  N20: R38.Pin_0, R_B.pin2
  N21: R38.Pin_1, R40.Pin_0, U1.P$2
  N22: R40.Pin_1, Q7.Pin_1
  N23: R39.Pin_0, R_B.pin1
  N24: R39.Pin_1, U1.P$1, D7.C
  N25: R41.Pin_0, Q7.Pin_2
  N26: R41.Pin_1, D7.A
  N27: M2.PIN_4, J79.pin2
  N28: M2.PIN_5, J79.pin1
  N29: J48.pin1, U2.D0_(RX)
  N30: J48.pin2, U2.D1_(TX)
  N31: RESET1.Pin_3, RESET1.Pin_4
  N32: PW2.pin1, G1.AC_IN#2
  N33: PW2.pin2, G1.AC_IN#1
  N34: R24.Pin_0, U2.D3_(PWM)
  N35: R24.Pin_1, M3.OUT+, D3.A, R27.Pin_1, BRST.Pin_1, R29.Pin_1
  N36: C1.+, D1.A, G1.DC_+
  N37: C1.-, ON/OFF_SW.C1, G1.DC_-
  N38: R9.Pin_0, R8.Pin_0, O1.+_Input_2
  N39: Q5.Pin_1, Q6.Pin_1, R19.Pin_0
  N40: Q5.Pin_2, U2.A0
  N41: Q5.Pin_4, Q6.Pin_4, R19.Pin_1, J2.pin3, O1.Vcc, C3.1, R7.Pin_1
  N42: Q5.Pin_3, R1.Pin_1
  N43: Q4.B, R1.Pin_0
  N44: Q4.C, J2.pin1
  N45: R2.Pin_0, Q6.Pin_3
  N46: R2.Pin_1, Q3.B
  N47: Q6.Pin_2, U2.D13
  N48: Q3.C, J2.pin2
  N49: R20.Pin_1, LED1.cathode
  N50: LED1.anode, U2.A5
  N51: R36.Pin_0, R_Y_B.pin3, R35.Pin_0, C14.2, PW1.pin1, PW1.pin3, Pad8.pad, Pad10.pad
  N52: R36.Pin_1, R35.Pin_1, Pad2.pad, Pad3.pad, Pad9.pad, G2.ac_input_2
  N53: R_Y_B.pin1, R34.Pin_1, Pad11.pad
  N54: R32.Pin_0, R33.Pin_0, Pad5.pad
  N55: R32.Pin_1, R37.Pin_0, C15.2, Pad12.pad, Pad13.pad
  N56: R33.Pin_1, R34.Pin_0, Pad4.pad, Pad6.pad
  N57: C14.1, C15.1
  N58: R37.Pin_1, Pad14.pad, G2.ac_input_1
  N59: Q9.G, Q2.C, R26.Pin_0
  N60: R42.Pin_0, Q7.Pin_3, J1_2.pin1, G2.dc_negative, C16.-
  N61: R42.Pin_1, J1_2.pin2, G2.dc_positive, C16.+
  N62: M3.IN+, R17.Pin_0, R18.Pin_0, J91.pin1, J91.pin2, M1.IN+, D1.C
  N63: M3.OUT-, R29.Pin_0
  N64: ON/OFF_SW.C2, Battery_SW.C1, Battery_SW.C2, J89.pin1, J89.pin2
  N65: R5.Pin_0, C17.1, J1.pin2
  N66: R5.Pin_1, O1.-_Input_2
  N67: Q7.Pin_4, J1_2.pin3
  N68: C17.0, J1.pin1
  N69: R17.Pin_1, R16.Pin_1, O1.+_Input_3
  N70: R13.Pin_1, O1.-_Input_3, R12.Pin_0
  N71: R16.Pin_0, D8.A, R15.Pin_0
  N72: O1.Output_2, R4.Pin_1
  N73: O1.Output_1, R6.Pin_0
  N74: O1.-_Input_1, D8.C, R11.Pin_0
  N75: O1.+_Input_1, R10.Pin_0, R15.Pin_1
  N76: O1.Output_3, R25.Pin_1
  N77: R4.Pin_0, C9.+, U2.D10_(PWM)
  N78: C9.-, C10.-
  N79: R6.Pin_1, U2.D9_(PWM), C10.+
  N80: R14.Pin_0, J58.pin3, U2.D7
  N81: R14.Pin_1, Q2.B, R27.Pin_0
  N82: Battery_SW.NO1, Battery_SW.NO2, Fuse1.C2, D4.A
  N83: J92.pin1, J92.pin2, M1.OUT+, D2.A
  N84: J58.pin1, U2.D5_(PWM)
  N85: J58.pin2, U2.D6_(PWM)
  N86: J58.pin4, U2.D8
  N87: U2.A2, J3.pin1
  N88: U2.A3, J3.pin2
  N89: U2.A4, J3.pin3
  N90: D2.C, M4.IN+
  N91: M4.B-, M4.OUT-
  N92: J2_2.pin1, D6.A, STOP.COIL2
  N93: J2_2.pin2, D5.A, START.COIL1
  N94: J2_2.pin3, D6.C, D5.C, STOP.COIL1, START.COIL2
  N95: STOP.A, S1_S2_N1_N2.pin4
  N96: STOP.C, START.C, S1_S2_N1_N2.pin1, S1_S2_N1_N2.pin3
  N97: START.A, S1_S2_N1_N2.pin2

notes:
  M-
  RX
  TX
  STX
  SRX
  1
  MOTOR
  FeedBack
  Battery
  _________________________________________
  ______________________________________________

custom parts:
  2PTH JST FROM HEADER 5: Generic rounded female header
  3pth XH JST Custom: 3PTH XH JST
  MOV: Metal Oxide Varistor
  MP1584 Step Down Module: Step Down Module based on MP1584
  Push Button Switch: DPDT On/Off Switch, when pressed connects NO to C.
  LM339: LM339 Quad Comparator IC. DIP14 Package.
  LM2596 Step Down Module: LM2596 Step Down Regulator
  Rectifier_6A: stand Up rectifier 6A
  TP4056 Lithium Ion Battery Charger: A lithium battery charging and powering shield.
  Fuse with Handler: Device used to protect against excessive current.
  Graetz Bridge Rectifier: Graetz Bridge Rectifier - znany także jako Mostek Graetz'a :)
